// Digital circuit 16BitRAM.dig as structural Verilog
module _16BitRAM (
  input  BusAIn8,
  input  BusAIn9,
  input  BusAIn10,
  input  BusAIn7,
  input  BusAIn6,
  input  BusAIn5,
  input  BusAIn4,
  input  BusAIn11,
  input  BusAIn12,
  input  BusAIn3,
  input  BusAIn2,
  input  BusAIn1,
  input  BusAIn13,
  input  BusAIn14,
  input  BusAIn15,
  input  BusAIn0,
  input  RAMInH,
  input  RAMInL,
  input  RAMOut,
  input  in_23,
  input  in_24,
  input  in_25,
  input  in_26,
  input  in_27,
  input  in_28,
  input  in_29,
  input  in_30,
  input  busOut,
  input  in_32,
  input  in_33,
  input  in_34,
  input  in_35,
  input  in_36,
  input  in_37,
  input  in_38,
  input  in_39,
  output SRAM,
  output FLASH,
  output PREF
);

  wire _16bitdisplayint_1_dec1, _16bitdisplayint_1_dec2, _16bitdisplayint_1_dec3, _16bitdisplayint_1_dec4,
       _74245_1_pin11, _74245_1_pin12, _74245_1_pin13, _74245_1_pin14, _74245_1_pin15, _74245_1_pin16,
       _74245_1_pin17, _74245_1_pin18, _74245_2_pin11, _74245_2_pin12, _74245_2_pin13, _74245_2_pin14,
       _74245_2_pin15, _74245_2_pin16, _74245_2_pin17, _74245_2_pin18;
  wire [3:0] _16bitdisplayint_1_digit1, _16bitdisplayint_1_digit2, _16bitdisplayint_1_digit3,
       _16bitdisplayint_1_digit4;
  wire [15:0] _16bitramint_1_display;

  _74245 _74245_1 (
    .pin1(1'b1), .pin2(in_30), .pin3(in_29), .pin4(in_28), .pin5(in_27), .pin6(in_26), .pin7(in_25),
    .pin8(in_24), .pin9(in_23), .pin10(1'b0), .pin11(_74245_1_pin11), .pin12(_74245_1_pin12),
    .pin13(_74245_1_pin13), .pin14(_74245_1_pin14), .pin15(_74245_1_pin15), .pin16(_74245_1_pin16),
    .pin17(_74245_1_pin17), .pin18(_74245_1_pin18), .pin19(busOut), .pin20(1'b1));
  LED Bus15 (.in(_74245_1_pin18));
  LED Bus13 (.in(_74245_1_pin16));
  LED Bus14 (.in(_74245_1_pin17));
  LED Bus11 (.in(_74245_1_pin14));
  LED Bus12 (.in(_74245_1_pin15));
  LED Bus9 (.in(_74245_1_pin12));
  LED Bus10 (.in(_74245_1_pin13));
  LED Bus8 (.in(_74245_1_pin11));
  _74245 _74245_2 (
    .pin1(1'b1), .pin2(in_39), .pin3(in_38), .pin4(in_37), .pin5(in_36), .pin6(in_35), .pin7(in_34),
    .pin8(in_33), .pin9(in_32), .pin10(1'b0), .pin11(_74245_2_pin11), .pin12(_74245_2_pin12),
    .pin13(_74245_2_pin13), .pin14(_74245_2_pin14), .pin15(_74245_2_pin15), .pin16(_74245_2_pin16),
    .pin17(_74245_2_pin17), .pin18(_74245_2_pin18), .pin19(busOut), .pin20(1'b1));
  LED Bus7 (.in(_74245_2_pin18));
  LED Bus5 (.in(_74245_2_pin16));
  LED Bus6 (.in(_74245_2_pin17));
  LED Bus3 (.in(_74245_2_pin14));
  LED Bus4 (.in(_74245_2_pin15));
  LED Bus1 (.in(_74245_2_pin12));
  LED Bus2 (.in(_74245_2_pin13));
  LED Bus0 (.in(_74245_2_pin11));
  _16BitRAMint _16bitramint_1 (
    .Sig15(_74245_1_pin18), .Sig14(_74245_1_pin17), .Sig13(_74245_1_pin16), .Sig12(_74245_1_pin15),
    .Sig11(_74245_1_pin14), .Sig10(_74245_1_pin13), .Sig9(_74245_1_pin12), .Sig8(_74245_1_pin11),
    .Sig7(_74245_2_pin18), .Sig6(_74245_2_pin17), .Sig5(_74245_2_pin16), .Sig4(_74245_2_pin15),
    .Sig3(_74245_2_pin14), .Sig2(_74245_2_pin13), .Sig1(_74245_2_pin12), .Sig0(_74245_2_pin11), .SRAM(SRAM),
    .FLASH(FLASH), .PREF(PREF), .RAMInH(RAMInH), .RAMInL(RAMInL), .RAMOut(RAMOut),
    .Display(_16bitramint_1_display),
    .ADDRin({BusAIn15, BusAIn14, BusAIn13, BusAIn12, BusAIn11, BusAIn10, BusAIn9, BusAIn8, BusAIn7, BusAIn6, BusAIn5, BusAIn4, BusAIn3, BusAIn2, BusAIn1, BusAIn0}));
  Seven_Seg_Hex seven_seg_hex_1 (.d(_16bitdisplayint_1_digit4), .dp(_16bitdisplayint_1_dec4));
  _16BitDisplayInt _16bitdisplayint_1 (
    .Digit4(_16bitdisplayint_1_digit4), .Dec4(_16bitdisplayint_1_dec4), .Digit3(_16bitdisplayint_1_digit3),
    .Dec3(_16bitdisplayint_1_dec3), .Digit2(_16bitdisplayint_1_digit2), .Dec2(_16bitdisplayint_1_dec2),
    .Digit1(_16bitdisplayint_1_digit1), .Dec1(_16bitdisplayint_1_dec1), .Input(_16bitramint_1_display));
  Seven_Seg_Hex seven_seg_hex_2 (.d(_16bitdisplayint_1_digit3), .dp(_16bitdisplayint_1_dec3));
  Seven_Seg_Hex seven_seg_hex_3 (.d(_16bitdisplayint_1_digit2), .dp(_16bitdisplayint_1_dec2));
  Seven_Seg_Hex seven_seg_hex_4 (.d(_16bitdisplayint_1_digit1), .dp(_16bitdisplayint_1_dec1));

  // Notes on the sheet:
  //   RAMInH: default 1
  //   RAMInL: default 1
  //   RAMOut: default 1
  //   busOut: default 1
endmodule
